# Fritzing sketch Plant_WatchDog (saved by Fritzing 0.9.4)
breadboards: 1

parts:
  Bauteil1 = Adafruit Feather nRF52840 Sense [part_number="Adafruit #4516"]
  VCC1 = Battery  # not connected
  Bauteil2 = Soil Moisture Sensor
  Bauteil3 = NeoPixel Stick [part_number=1426]

nets:
  3.3V: Bauteil1.3.3V, Bauteil2.VCC, Bauteil3.+5V
  GND: Bauteil1.GND, Bauteil2.GND, Bauteil3.GND
  N1: Bauteil1.A0, Bauteil2.SIG
  N2: Bauteil1.D9, Bauteil3.DATAIN

custom parts:
  Adafruit Feather nRF52840 Sense: The Adafruit Feather Bluefruit Sense takes our popular Feather nRF52840 Express and adds a smorgasbord of sensors to make a great wireless sensor platform. This Feather microcontroller comes with Bluetooth Low Energy and native USB support featuring the nRF52840! This Feather is an 'all-in-one' Arduino-compatible + Bluetooth Low Energy with built in USB plus battery charging. With native USB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
  NeoPixel Stick: Make your own little LED strip arrangement with this stick of NeoPixel LEDs. We crammed 8 of the tiny 5050 (5mm x 5mm) smart RGB LEDs onto a PCB with mounting holes and a chainable design. Use only one microcontroller pin to control as many as you can chain together! Each LED is addressable as the driver chip is inside the LED. Each one has ~18mA constant current drive so the color will be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
